// Logisim project Somador_4bits.circ as structural Verilog: 10 circuits, main circuit main
module main (
  input  a3,
  input  a2,
  input  a1,
  input  a0,
  input  Cin,
  input  b3,
  input  b2,
  input  b1,
  input  b0,
  output s0,
  output s1,
  output s2,
  output s3,
  output Cout,
  output overflow
);

  wire decodificador_hexa_1_a, decodificador_hexa_1_b, decodificador_hexa_1_c, decodificador_hexa_1_d,
       decodificador_hexa_1_e, decodificador_hexa_1_f, decodificador_hexa_1_g, decodificador_hexa_2_a,
       decodificador_hexa_2_b, decodificador_hexa_2_c, decodificador_hexa_2_d, decodificador_hexa_2_e,
       decodificador_hexa_2_f, decodificador_hexa_2_g, decodificador_hexa_3_a, decodificador_hexa_3_b,
       decodificador_hexa_3_c, decodificador_hexa_3_d, decodificador_hexa_3_e, decodificador_hexa_3_f,
       decodificador_hexa_3_g;

  decodificador_hexa decodificador_hexa_1 (
    .A0(a3), .A1(a2), .A2(a1), .A3(a0), .a(decodificador_hexa_1_a), .b(decodificador_hexa_1_b),
    .c(decodificador_hexa_1_c), .d(decodificador_hexa_1_d), .e(decodificador_hexa_1_e),
    .f(decodificador_hexa_1_f), .g(decodificador_hexa_1_g));
  somador_4bits somador_4bits_1 (
    .x0(a0), .y0(b0), .x1(a1), .y1(b1), .x2(a2), .y2(b2), .x3(a3), .y3(b3), .Vai1(Cout), .in_1(Cin), .S0(s0),
    .S1(s1), .S2(s2), .S3(s3), .overflow(overflow));
  decodificador_hexa decodificador_hexa_2 (
    .A0(b3), .A1(b2), .A2(b1), .A3(b0), .a(decodificador_hexa_2_a), .b(decodificador_hexa_2_b),
    .c(decodificador_hexa_2_c), .d(decodificador_hexa_2_d), .e(decodificador_hexa_2_e),
    .f(decodificador_hexa_2_f), .g(decodificador_hexa_2_g));
  _7_Segment_Display u_7_segment_display_1 (
    .g(decodificador_hexa_1_g), .f(decodificador_hexa_1_f), .a(decodificador_hexa_1_a),
    .b(decodificador_hexa_1_b), .e(decodificador_hexa_1_e), .d(decodificador_hexa_1_d),
    .c(decodificador_hexa_1_c));  // open: dp
  _7_Segment_Display u_7_segment_display_2 (
    .g(decodificador_hexa_2_g), .f(decodificador_hexa_2_f), .a(decodificador_hexa_2_a),
    .b(decodificador_hexa_2_b), .e(decodificador_hexa_2_e), .d(decodificador_hexa_2_d),
    .c(decodificador_hexa_2_c));  // open: dp
  decodificador_hexa decodificador_hexa_3 (
    .A0(s3), .A1(s2), .A2(s1), .A3(s0), .a(decodificador_hexa_3_a), .b(decodificador_hexa_3_b),
    .c(decodificador_hexa_3_c), .d(decodificador_hexa_3_d), .e(decodificador_hexa_3_e),
    .f(decodificador_hexa_3_f), .g(decodificador_hexa_3_g));
  _7_Segment_Display u_7_segment_display_3 (
    .g(decodificador_hexa_3_g), .f(decodificador_hexa_3_f), .a(decodificador_hexa_3_a),
    .b(decodificador_hexa_3_b), .e(decodificador_hexa_3_e), .d(decodificador_hexa_3_d),
    .c(decodificador_hexa_3_c));  // open: dp
endmodule

module meia_soma (
  input  x,
  input  y,
  output S,
  output Vai1
);

  xor xor_1 (S, x, y);
  and and_1 (Vai1, y, x);
endmodule

module soma_completa (
  input  Cin,
  input  X1,
  input  X2,
  output Soma,
  output Vai1
);

  wire meia_soma_1_s, meia_soma_1_vai1, meia_soma_2_vai1;

  meia_soma meia_soma_1 (.x(X1), .y(X2), .S(meia_soma_1_s), .Vai1(meia_soma_1_vai1));
  or or_1 (Vai1, meia_soma_1_vai1, meia_soma_2_vai1);
  meia_soma meia_soma_2 (.x(Cin), .y(meia_soma_1_s), .S(Soma), .Vai1(meia_soma_2_vai1));
endmodule

module decodificador_hexa (
  input  A0,
  input  A1,
  input  A2,
  input  A3,
  output a,
  output b,
  output c,
  output d,
  output e,
  output f,
  output g
);

  wire and_1_out, and_2_out, and_3_out, and_4_out, and_5_out, and_6_out, and_7_out, and_8_out, and_9_out,
       and_10_out, and_11_out, and_12_out, and_13_out, and_14_out, and_15_out, and_16_out, and_17_out,
       and_18_out, and_19_out, and_20_out, and_21_out, and_22_out, and_23_out, and_24_out, and_25_out,
       and_26_out, and_27_out, and_28_out, and_29_out, and_30_out, and_31_out, and_32_out, and_33_out,
       and_34_out, and_35_out, not_1_out, not_2_out, not_3_out, not_4_out, not_5_out, not_6_out, not_7_out,
       not_8_out, not_9_out, not_10_out, not_11_out, not_12_out, not_13_out, not_14_out, not_15_out,
       not_16_out, not_17_out, not_18_out, not_19_out, not_20_out, not_21_out, not_22_out, not_23_out,
       not_24_out, not_25_out, not_26_out, not_27_out, not_28_out, not_29_out, not_30_out, not_31_out,
       not_32_out, not_33_out, not_34_out, not_35_out, not_36_out, not_37_out, not_38_out, not_39_out,
       not_40_out, not_41_out, not_42_out, not_43_out, not_44_out;

  not not_1 (not_1_out, A1);
  and and_1 (and_1_out, not_1_out, not_2_out);
  not not_2 (not_2_out, A3);
  not not_3 (not_3_out, A0);
  and and_2 (and_2_out, not_3_out, A2);
  not not_4 (not_4_out, A0);
  and and_3 (and_3_out, not_4_out, A1, A3);
  and and_4 (and_4_out, A1, A2);
  not not_5 (not_5_out, A1);
  and and_5 (and_5_out, A0, not_5_out, not_6_out);
  not not_6 (not_6_out, A2);
  and and_6 (and_6_out, A0, not_7_out);
  not not_7 (not_7_out, A3);
  not not_8 (not_8_out, A0);
  and and_7 (and_7_out, not_8_out, not_9_out);
  not not_9 (not_9_out, A1);
  not not_10 (not_10_out, A0);
  and and_8 (and_8_out, not_10_out, not_11_out, not_12_out);
  not not_11 (not_11_out, A2);
  not not_12 (not_12_out, A3);
  not not_13 (not_13_out, A1);
  and and_9 (and_9_out, not_13_out, not_14_out);
  not not_14 (not_14_out, A3);
  not not_15 (not_15_out, A0);
  and and_10 (and_10_out, not_15_out, A2, A3);
  and and_11 (and_11_out, A0, not_16_out, A3);
  not not_16 (not_16_out, A2);
  not not_17 (not_17_out, A0);
  and and_12 (and_12_out, not_17_out, not_18_out);
  not not_18 (not_18_out, A2);
  not not_19 (not_19_out, A0);
  and and_13 (and_13_out, not_19_out, A3);
  not not_20 (not_20_out, A2);
  and and_14 (and_14_out, not_20_out, A3);
  not not_21 (not_21_out, A0);
  and and_15 (and_15_out, not_21_out, A1);
  and and_16 (and_16_out, A0, not_22_out);
  not not_22 (not_22_out, A1);
  not not_23 (not_23_out, A0);
  not not_24 (not_24_out, A1);
  and and_17 (and_17_out, not_23_out, not_24_out, not_25_out);
  not not_25 (not_25_out, A3);
  not not_26 (not_26_out, A1);
  and and_18 (and_18_out, not_26_out, A2, A3);
  not not_27 (not_27_out, A2);
  and and_19 (and_19_out, A1, not_27_out, A3);
  and and_20 (and_20_out, A1, A2, not_28_out);
  not not_28 (not_28_out, A3);
  and and_21 (and_21_out, A0, not_29_out, not_30_out);
  not not_29 (not_29_out, A2);
  not not_30 (not_30_out, A3);
  not not_31 (not_31_out, A1);
  and and_22 (and_22_out, not_31_out, not_32_out);
  not not_32 (not_32_out, A3);
  and and_23 (and_23_out, A2, not_33_out);
  not not_33 (not_33_out, A3);
  and and_24 (and_24_out, A0, A2);
  and and_25 (and_25_out, A0, A1);
  not not_34 (not_34_out, A2);
  and and_26 (and_26_out, not_34_out, not_35_out);
  not not_35 (not_35_out, A3);
  not not_36 (not_36_out, A0);
  and and_27 (and_27_out, not_36_out, A1, not_37_out);
  not not_37 (not_37_out, A2);
  and and_28 (and_28_out, A1, not_38_out);
  not not_38 (not_38_out, A3);
  and and_29 (and_29_out, A0, not_39_out);
  not not_39 (not_39_out, A1);
  and and_30 (and_30_out, A0, A2);
  not not_40 (not_40_out, A1);
  and and_31 (and_31_out, not_40_out, A2);
  and and_32 (and_32_out, A2, not_41_out);
  not not_41 (not_41_out, A3);
  not not_42 (not_42_out, A0);
  and and_33 (and_33_out, not_42_out, A1, not_43_out);
  not not_43 (not_43_out, A2);
  and and_34 (and_34_out, A0, not_44_out);
  not not_44 (not_44_out, A1);
  and and_35 (and_35_out, A0, A3);
  or or_1 (b, and_7_out, and_8_out, and_9_out, and_10_out, and_11_out);
  or or_2 (c, and_12_out, and_13_out, and_14_out, and_15_out, and_16_out);
  or or_3 (d, and_17_out, and_18_out, and_19_out, and_20_out, and_21_out);
  or or_4 (e, and_22_out, and_23_out, and_24_out, and_25_out);
  or or_5 (f, and_26_out, and_27_out, and_28_out, and_29_out, and_30_out);
  or or_6 (g, and_31_out, and_32_out, and_33_out, and_34_out, and_35_out);
  or or_7 (a, and_1_out, and_2_out, and_3_out, and_4_out, and_5_out, and_6_out);
endmodule

module somador_4bits (
  input  in_1,
  input  x0,
  input  y0,
  input  x1,
  input  y1,
  input  x2,
  input  y2,
  input  x3,
  input  y3,
  output S0,
  output S1,
  output S2,
  output S3,
  output overflow,
  output Vai1
);

  wire soma_completa_1_vai1, soma_completa_2_vai1, soma_completa_3_vai1;

  soma_completa soma_completa_1 (.X1(x0), .X2(y0), .Cin(in_1), .Vai1(soma_completa_1_vai1), .Soma(S0));
  soma_completa soma_completa_2 (.X1(x1), .X2(y1), .Cin(soma_completa_1_vai1), .Vai1(soma_completa_2_vai1), .Soma(S1));
  soma_completa soma_completa_3 (.X1(x2), .X2(y2), .Cin(soma_completa_2_vai1), .Vai1(soma_completa_3_vai1), .Soma(S2));
  soma_completa soma_completa_4 (.X1(x3), .X2(y3), .Cin(soma_completa_3_vai1), .Vai1(Vai1), .Soma(S3));
  xor xor_1 (overflow, soma_completa_3_vai1, Vai1);
endmodule

module MUX (
  input  m,
  input  n,
  input  Sel,
  output S
);

  wire and_1_out, and_2_out, not_1_out;

  not not_1 (not_1_out, Sel);
  and and_1 (and_1_out, m, not_1_out);
  and and_2 (and_2_out, n, Sel);
  or or_1 (S, and_1_out, and_2_out);
endmodule

module MUX2_bits (
  input  \and ,
  input  \or ,
  input  \not ,
  input  soma,
  input  op1,
  input  op0,
  output x
);

  wire and_1_out, and_2_out, and_3_out, and_4_out, not_1_out, not_2_out, not_3_out, not_4_out;

  not not_1 (not_1_out, op1);
  not not_2 (not_2_out, op0);
  not not_3 (not_3_out, op1);
  not not_4 (not_4_out, op0);
  and and_1 (and_1_out, \and , not_1_out, not_2_out);
  and and_2 (and_2_out, \or , not_3_out, op0);
  and and_3 (and_3_out, \not , op1, not_4_out);
  and and_4 (and_4_out, soma, op1, op0);
  or or_1 (x, and_1_out, and_2_out, and_3_out, and_4_out);
endmodule

module ULA_1bit (
  input  A,
  input  B,
  input  op1,
  input  op0,
  input  Cin,
  input  Binverter,
  output S,
  output Cout
);

  wire and_1_out, mux_s, not_1_out, not_2_out, or_1_out, somador_soma;

  not not_1 (not_1_out, B);
  MUX mux (.m(B), .n(not_1_out), .Sel(Binverter), .S(mux_s));
  and and_1 (and_1_out, A, B);
  or or_1 (or_1_out, A, B);
  not not_2 (not_2_out, A);
  soma_completa somador (.X1(A), .X2(mux_s), .Cin(Cin), .Vai1(Cout), .Soma(somador_soma));
  MUX2_bits mux_2bits (
    .\and (and_1_out), .\or (or_1_out), .\not (not_2_out), .soma(somador_soma), .op1(op1), .op0(op0), .x(S));
endmodule

module ULA_4bits (
  input  Binvert,
  input  b3,
  input  b2,
  input  b1,
  input  b0,
  input  a3,
  input  a2,
  input  a1,
  input  a0,
  input  op1,
  input  op0,
  output s0,
  output s1,
  output s2,
  output s3
);

  wire ULA_0_cout, ULA_1_cout, ULA_2_cout;

  ULA_1bit ULA_0 (.A(a0), .B(b0), .Cin(Binvert), .S(s0), .Binverter(Binvert), .Cout(ULA_0_cout), .op1(op1), .op0(op0));
  ULA_1bit ULA_1 (
    .A(a1), .B(b1), .Cin(ULA_0_cout), .S(s1), .Binverter(Binvert), .Cout(ULA_1_cout), .op1(op1), .op0(op0));
  ULA_1bit ULA_2 (
    .A(a2), .B(b2), .Cin(ULA_1_cout), .S(s2), .Binverter(Binvert), .Cout(ULA_2_cout), .op1(op1), .op0(op0));
  ULA_1bit ULA_3 (.A(a3), .B(b3), .Cin(ULA_2_cout), .S(s3), .Binverter(Binvert), .op1(op1), .op0(op0));  // open: Cout
endmodule

module ULA_2 (
  input  [3:0] a,
  input  [3:0] b,
  input  [3:0] S,
  output [3:0] f
);

  wire [3:0] and_1_out, and_2_out, and_3_out, nand_1_out, nor_1_out, not_1_out, not_2_out, not_3_out,
       not_4_out, not_5_out, not_6_out, not_7_out, not_8_out, not_9_out, or_1_out, or_2_out, or_3_out,
       xor_1_out, xor_2_out;

  assign not_1_out = ~b;  // NOT_Gate not_1, 4 bits wide
  assign not_2_out = ~b;  // NOT_Gate not_2, 4 bits wide
  assign not_3_out = ~a;  // NOT_Gate not_3, 4 bits wide
  assign not_4_out = ~b;  // NOT_Gate not_4, 4 bits wide
  assign not_5_out = ~a;  // NOT_Gate not_5, 4 bits wide
  assign not_6_out = ~b;  // NOT_Gate not_6, 4 bits wide
  assign and_1_out = a & b;  // AND_Gate and_1, 4 bits wide
  assign or_1_out = a | not_1_out;  // OR_Gate or_1, 4 bits wide
  assign or_2_out = a | b;  // OR_Gate or_2, 4 bits wide
  assign not_7_out = ~a;  // NOT_Gate not_7, 4 bits wide
  assign xor_1_out = a ^ b;  // XOR_Gate xor_1, 4 bits wide
  assign and_2_out = a & not_2_out;  // AND_Gate and_2, 4 bits wide
  assign or_3_out = not_3_out | not_4_out;  // OR_Gate or_3, 4 bits wide
  assign xor_2_out = not_5_out ^ not_6_out;  // XOR_Gate xor_2, 4 bits wide
  assign nand_1_out = ~(a & b);  // NAND_Gate nand_1, 4 bits wide
  assign and_3_out = not_7_out & b;  // AND_Gate and_3, 4 bits wide
  assign nor_1_out = ~(a | a);  // NOR_Gate nor_1, 4 bits wide
  assign not_8_out = ~a;  // NOT_Gate not_8, 4 bits wide
  assign not_9_out = ~b;  // NOT_Gate not_9, 4 bits wide
  Multiplexer #(.select(4), .width(4)) multiplexer_1 (
    .in0(not_9_out), .in1(nand_1_out), .in2(and_3_out), .in3(4'b0000), .in4(nor_1_out), .in5(not_8_out),
    .in6(xor_1_out), .in7(and_2_out), .in8(or_3_out), .in9(xor_2_out), .in10(b), .in11(and_1_out),
    .in12(4'b1111), .in13(or_1_out), .in14(or_2_out), .in15(a), .out(f), .sel(S));  // open: en
endmodule
